# Fritzing sketch IIoT_Project_Circuit (saved by Fritzing 1.0.5)
breadboards: 1

parts:
  S1 = Pushbutton [package="[THT]"]
  S2 = Pushbutton [package="[THT]"]
  LED1 = Blue LED - Rect 5x2x7mm [package="5x2x7 mm [THT]"]
  LED2 = Yellow LED - Rect 5x2x7mm [package="5x2x7 mm [THT]"]
  Mod1 = Amica NodeMCU DEVKIT 1.0
  DHT1 = DHT11 Humitidy and Temperature Sensor (3 pins)
  e-radionica_com1 = LM393 LDR breakout [part_number=100027]
  S3 = Pushbutton [package="[SMD]"]
  S4 = Pushbutton [package="[SMD]"]
  S5 = H-Bridge with L298N
  M1 = DC Motor [voltage_(max)=6V voltage_(min)=3V]

nets:
  GND: S1.Pin_1, S1.Pin_2, S2.Pin_1, S2.Pin_2, LED1.anode, LED2.anode, DHT1.Gnd, e-radionica_com1.GND, S3.Pin_1, S3.Pin_2, S4.Pin_1, S4.Pin_2
  N1: S1.Pin_3, S1.Pin_4, Mod1.pin8
  N2: S2.Pin_3, S2.Pin_4, Mod1.pin_13
  N3: LED1.cathode, Mod1.pin7
  N4: LED2.cathode, Mod1.pin6
  N5: Mod1.pin1, Mod1.pin_10, Mod1.pin_26
  N6: Mod1.pin2, Mod1.pin_9, Mod1.pin_25, Mod1.pin_29
  N7: Mod1.pin5, DHT1.Signal
  N8: Mod1.pin_11, S3.Pin_3, S3.Pin_4
  N9: Mod1.pin_12, S4.Pin_3, S4.Pin_4
  N10: Mod1.pin_14, S5.IN2
  N11: Mod1.pin_15, S5.IN1
  N12: Mod1.pin_16, e-radionica_com1.AO
  N13: DHT1.Plus, e-radionica_com1.VCC
  N14: S5.M2-01, M1.pin_2
  N15: S5.M2-02, M1.pin_1

custom parts:
  Blue LED - Rect 5x2x7mm: A generic rectangular blue LED (~1.8V) 5mm x 2mm x 7mm
  Yellow LED - Rect 5x2x7mm: A generic rectangular yellow LED (~1.8V) 5mm x 2mm x 7mm
  DHT11 Humitidy and Temperature Sensor (3 pins): DHT11 Humidity and Temperature Sensor (3 pins).
  H-Bridge with L298N: h-bridge
